// Logisim project 1_bit_alu.circ as structural Verilog
module main (
  input  Binvert,
  input  Ainvert,
  input  A,
  input  B,
  input  Cin,
  input  [1:0] Op,
  output Result,
  output Cout
);

  wire and_1_out, and_2_out, and_3_out, and_4_out, multiplexer_1_out, multiplexer_2_out, not_1_out,
       not_2_out, or_1_out, undriven, xor_1_out, xor_2_out;

  not not_1 (not_1_out, A);
  not not_2 (not_2_out, B);
  Multiplexer multiplexer_1 (.in0(A), .in1(not_1_out), .out(multiplexer_1_out), .sel(Ainvert));
  Multiplexer multiplexer_2 (.in0(B), .in1(not_2_out), .out(multiplexer_2_out), .sel(Binvert));
  and and_1 (and_1_out, multiplexer_1_out, multiplexer_2_out);
  or or_1 (or_1_out, multiplexer_1_out, multiplexer_2_out);
  xor xor_1 (xor_1_out, multiplexer_1_out, multiplexer_2_out);
  and and_2 (and_2_out, Cin, multiplexer_1_out);
  and and_3 (and_3_out, Cin, multiplexer_2_out);
  and and_4 (and_4_out, multiplexer_1_out, multiplexer_2_out);
  xor xor_2 (xor_2_out, xor_1_out, Cin);
  or or_2 (Cout, and_2_out, and_3_out, and_4_out);
  Multiplexer #(.select(2)) multiplexer_3 (
    .in0(and_1_out), .in1(or_1_out), .in2(xor_2_out), .in3(undriven), .out(Result), .sel(Op));

  // Notes on the sheet:
  //   00 - AND
  //   01 - OR
  //   10 - SUM
endmodule

module ALU2 (
);

  ALU1 alu1_1 ();
  ALU1 alu1_2 ();
endmodule
