// Logisim project ALU_ALL.circ as structural Verilog: 11 circuits, main circuit main
module main (
  input  [1:0] Op,
  input  [31:0] A,
  input  [31:0] B,
  output [31:0] out_4,
  output out_5
);

  wire alu8_1_carryout, alu8_2_carryout, alu8_3_carryout;

  Register register_1 ();  // open: D, en, clk, Q, clr
  Register register_2 ();  // open: D, en, clk, Q, clr
  RAM ram_1 ();  // open: addr, we, oe, clk, din, dout
  ALU8 alu8_1 (.CarryIn(1'b0), .A(A[7:0]), .B(B[7:0]), .OpCode(Op), .CarryOut(alu8_1_carryout), .Result(out_4[7:0]));
  ALU8 alu8_2 (
    .CarryIn(alu8_1_carryout), .A(A[15:8]), .B(B[15:8]), .OpCode(Op), .CarryOut(alu8_2_carryout),
    .Result(out_4[15:8]));
  ALU8 alu8_3 (
    .CarryIn(alu8_2_carryout), .A(A[23:16]), .B(B[23:16]), .OpCode(Op), .CarryOut(alu8_3_carryout),
    .Result(out_4[23:16]));
  ALU8 alu8_4 (
    .CarryIn(alu8_3_carryout), .A(A[31:24]), .B(B[31:24]), .OpCode(Op), .CarryOut(out_5),
    .Result(out_4[31:24]));
  RAM ram_2 ();  // open: addr, we, oe, clk, din, dout
  Register register_3 ();  // open: D, en, clk, Q, clr
  Register register_4 ();  // open: D, en, clk, Q, clr
endmodule

module half_adder (
  input  A,
  input  B,
  output Carry,
  output Sum
);

  wire and_1_out, and_2_out, not_1_out, not_2_out;

  not not_1 (not_1_out, A);
  not not_2 (not_2_out, B);
  and and_1 (and_1_out, not_1_out, B);
  and and_2 (and_2_out, A, not_2_out);
  and and_3 (Carry, A, B);
  or or_1 (Sum, and_1_out, and_2_out);
endmodule

module full_adder (
  input  A,
  input  B,
  input  CarryIn,
  output CarryOut,
  output Sum
);

  wire half_adder_1_carry, half_adder_1_sum, half_adder_2_carry;

  half_adder half_adder_1 (.A(A), .B(B), .Carry(half_adder_1_carry), .Sum(half_adder_1_sum));
  half_adder half_adder_2 (.A(half_adder_1_sum), .B(CarryIn), .Carry(half_adder_2_carry), .Sum(Sum));
  or or_1 (CarryOut, half_adder_1_carry, half_adder_2_carry);
endmodule

module ALU (
  input  CarryIn,
  input  B,
  input  A,
  input  [1:0] Operation,
  output Result,
  output CarryOut
);

  wire and_1_out, full_adder_1_sum, or_1_out;

  and and_1 (and_1_out, A, B);
  or or_1 (or_1_out, A, B);
  full_adder full_adder_1 (.A(A), .B(B), .CarryIn(CarryIn), .CarryOut(CarryOut), .Sum(full_adder_1_sum));
  Multiplexer #(.select(2)) multiplexer_1 (
    .in0(and_1_out), .in1(or_1_out), .in2(full_adder_1_sum), .out(Result), .sel(Operation));  // open: in3

  // Notes on the sheet:
  //   Operation 00 is Logical AND
  //   Operation 01 is Logical OR
  //   Operation 10 is Addition
endmodule

module Adder_4bits (
  input  CarryIn,
  input  B3,
  input  B2,
  input  B1,
  input  B0,
  input  A3,
  input  A2,
  input  A1,
  input  A0,
  output Cout,
  output Sum3,
  output Sum2,
  output Sum1,
  output Sum0
);

  wire full_adder_1_carryout, full_adder_2_carryout, full_adder_3_carryout;

  full_adder full_adder_1 (.A(A0), .B(B0), .CarryIn(CarryIn), .CarryOut(full_adder_1_carryout), .Sum(Sum0));
  full_adder full_adder_2 (
    .A(A1), .B(B1), .CarryIn(full_adder_1_carryout), .CarryOut(full_adder_2_carryout), .Sum(Sum1));
  full_adder full_adder_3 (
    .A(A2), .B(B2), .CarryIn(full_adder_2_carryout), .CarryOut(full_adder_3_carryout), .Sum(Sum2));
  full_adder full_adder_4 (.A(A3), .B(B3), .CarryIn(full_adder_3_carryout), .CarryOut(Cout), .Sum(Sum3));
endmodule

module Adder_4bits_BCD (
  input  [3:0] A,
  input  [3:0] B
);

  wire binary_to_bcd_converter_1_p2, binary_to_bcd_converter_1_p4;
  wire [4:0] adder_4bits_1_sum0;

  Adder_4bits adder_4bits_1 (
    .CarryIn(1'b0), .B3(B[3]), .B2(B[2]), .B1(B[1]), .B0(B[0]), .A3(A[3]), .A2(A[2]), .A1(A[1]), .A0(A[0]),
    .Cout(adder_4bits_1_sum0[4]), .Sum3(adder_4bits_1_sum0[3]), .Sum2(adder_4bits_1_sum0[2]),
    .Sum1(adder_4bits_1_sum0[1]), .Sum0(adder_4bits_1_sum0[0]));
  _7_Segment_Display u_7_segment_display_1 ();  // open: g, f, a, b, e, d, c, dp
  // BCD_to_7_Segment_decoder bcd_to_7_segment_decoder_1: pin names not known
  // Binary_to_BCD_converter #(.binvalue(5)) binary_to_bcd_converter_1: pin names not known; wires that end beside it: adder_4bits_1_sum0, binary_to_bcd_converter_1_p2, binary_to_bcd_converter_1_p2, binary_to_bcd_converter_1_p4
  _7_Segment_Display u_7_segment_display_2 ();  // open: g, f, a, b, e, d, c, dp
  // BCD_to_7_Segment_decoder bcd_to_7_segment_decoder_2: pin names not known; wires that end beside it: binary_to_bcd_converter_1_p4
endmodule

module ALU4 (
  input  CarryIn,
  input  [3:0] A,
  input  [3:0] B,
  input  [1:0] OpCode,
  output CarryOut,
  output [3:0] Result
);

  wire alu_1_carryout, alu_2_carryout, alu_3_carryout;

  ALU alu_1 (.CarryIn(CarryIn), .B(B[0]), .A(A[0]), .Operation(OpCode), .Result(Result[0]), .CarryOut(alu_1_carryout));
  ALU alu_2 (
    .CarryIn(alu_1_carryout), .B(B[1]), .A(A[1]), .Operation(OpCode), .Result(Result[1]),
    .CarryOut(alu_2_carryout));
  ALU alu_3 (
    .CarryIn(alu_2_carryout), .B(B[2]), .A(A[2]), .Operation(OpCode), .Result(Result[2]),
    .CarryOut(alu_3_carryout));
  ALU alu_4 (.CarryIn(alu_3_carryout), .B(B[3]), .A(A[3]), .Operation(OpCode), .Result(Result[3]), .CarryOut(CarryOut));

  // Notes on the sheet:
  //   Operation 00 is Logical AND
  //   Operation 01 is Logical OR
  //   Operation 10 is Addition
endmodule

module Adder_4bits_Rev (
  input  CarryIn,
  input  B3,
  input  B2,
  input  B1,
  input  B0,
  input  A3,
  input  A2,
  input  A1,
  input  A0,
  output Cout,
  output Sum3,
  output Sum2,
  output Sum1,
  output Sum0
);

  wire and_1_out, and_2_out, and_3_out, and_4_out, and_5_out, and_6_out, bcd_to_7_segment_decoder_2_p1,
       binary_to_bcd_converter_1_p2, C1, C2, C3;

  and and_1 (and_1_out, C1, B1);
  and and_2 (and_2_out, C1, A1);
  and and_3 (and_3_out, A1, B1);
  or or_1 (C2, and_1_out, and_2_out, and_3_out);
  and u_C1 (C1, A0, B0);
  and and_4 (and_4_out, C2, B2);
  and and_5 (and_5_out, C2, A2);
  and and_6 (and_6_out, A2, B2);
  or or_2 (C3, and_4_out, and_5_out, and_6_out);
  full_adder full_adder_1 (.A(A0), .B(B0), .CarryIn(CarryIn), .Sum(Sum0));  // open: CarryOut
  full_adder full_adder_2 (.A(A1), .B(B1), .CarryIn(C1), .Sum(Sum1));  // open: CarryOut
  full_adder full_adder_3 (.A(A2), .B(B2), .CarryIn(C2), .Sum(Sum2));  // open: CarryOut
  full_adder full_adder_4 (.A(A3), .B(B3), .CarryIn(C3), .CarryOut(Cout), .Sum(Sum3));
  _7_Segment_Display u_7_segment_display_1 ();  // open: g, f, a, b, e, d, c, dp
  _7_Segment_Display u_7_segment_display_2 ();  // open: g, f, a, b, e, d, c, dp
  // BCD_to_7_Segment_decoder bcd_to_7_segment_decoder_1: pin names not known
  // BCD_to_7_Segment_decoder bcd_to_7_segment_decoder_2: pin names not known; wires that end beside it: bcd_to_7_segment_decoder_2_p1
  // Binary_to_BCD_converter #(.binvalue(5)) binary_to_bcd_converter_1: pin names not known; wires that end beside it: {Cout, Sum3, Sum2, Sum1, Sum0}, binary_to_bcd_converter_1_p2, binary_to_bcd_converter_1_p2, bcd_to_7_segment_decoder_2_p1
endmodule

module Adder_8bits (
  input  CarryIn,
  input  [7:0] A,
  input  [7:0] B,
  output Carryout,
  output [7:0] Sum
);

  wire adder_4bits_1_cout, bcd_to_7_segment_decoder_2_p1, bcd_to_7_segment_decoder_3_p1,
       binary_to_bcd_converter_1_p2;

  Adder_4bits adder_4bits_1 (
    .CarryIn(CarryIn), .B3(B[3]), .B2(B[2]), .B1(B[1]), .B0(B[0]), .A3(A[3]), .A2(A[2]), .A1(A[1]),
    .A0(A[0]), .Cout(adder_4bits_1_cout), .Sum3(Sum[3]), .Sum2(Sum[2]), .Sum1(Sum[1]), .Sum0(Sum[0]));
  Adder_4bits adder_4bits_2 (
    .CarryIn(adder_4bits_1_cout), .B3(B[7]), .B2(B[6]), .B1(B[5]), .B0(B[4]), .A3(A[7]), .A2(A[6]),
    .A1(A[5]), .A0(A[4]), .Cout(Carryout), .Sum3(Sum[7]), .Sum2(Sum[6]), .Sum1(Sum[5]), .Sum0(Sum[4]));
  _7_Segment_Display u_7_segment_display_1 ();  // open: g, f, a, b, e, d, c, dp
  // BCD_to_7_Segment_decoder bcd_to_7_segment_decoder_1: pin names not known
  _7_Segment_Display u_7_segment_display_2 ();  // open: g, f, a, b, e, d, c, dp
  // BCD_to_7_Segment_decoder bcd_to_7_segment_decoder_2: pin names not known; wires that end beside it: bcd_to_7_segment_decoder_2_p1
  // Binary_to_BCD_converter binary_to_bcd_converter_1: pin names not known; wires that end beside it: {Carryout, Sum}, binary_to_bcd_converter_1_p2, binary_to_bcd_converter_1_p2, bcd_to_7_segment_decoder_2_p1
  _7_Segment_Display u_7_segment_display_3 ();  // open: g, f, a, b, e, d, c, dp
  // BCD_to_7_Segment_decoder bcd_to_7_segment_decoder_3: pin names not known; wires that end beside it: bcd_to_7_segment_decoder_3_p1, bcd_to_7_segment_decoder_3_p1
endmodule

module Adder_16bits (
  input  CarryIn,
  input  [15:0] A,
  input  [15:0] B,
  output CarryOut,
  output [15:0] Sum
);

  wire adder_8bits_1_carryout;

  Adder_8bits adder_8bits_1 (
    .CarryIn(CarryIn), .A(A[7:0]), .B(B[7:0]), .Carryout(adder_8bits_1_carryout), .Sum(Sum[7:0]));
  Adder_8bits adder_8bits_2 (
    .CarryIn(adder_8bits_1_carryout), .A(A[15:8]), .B(B[15:8]), .Carryout(CarryOut), .Sum(Sum[15:8]));
endmodule

module ALU8 (
  input  CarryIn,
  input  [7:0] A,
  input  [7:0] B,
  input  [1:0] OpCode,
  output CarryOut,
  output [7:0] Result
);

  wire alu4_1_carryout, n7_segment_display_1_p1, n7_segment_display_2_p1, n7_segment_display_3_p1;

  ALU4 alu4_1 (
    .CarryIn(CarryIn), .A(A[3:0]), .B(B[3:0]), .OpCode(OpCode), .CarryOut(alu4_1_carryout),
    .Result(Result[3:0]));
  ALU4 alu4_2 (
    .CarryIn(alu4_1_carryout), .A(A[7:4]), .B(B[7:4]), .OpCode(OpCode), .CarryOut(CarryOut),
    .Result(Result[7:4]));
  // _7_Segment_Display 7_segment_display_1: pin names not known; wires that end beside it: n7_segment_display_1_p1, n7_segment_display_1_p1
  // BCD_to_7_Segment_decoder bcd_to_7_segment_decoder_1: pin names not known
  // Binary_to_BCD_converter binary_to_bcd_converter_1: pin names not known; wires that end beside it: {CarryOut, Result}
  // _7_Segment_Display 7_segment_display_2: pin names not known; wires that end beside it: n7_segment_display_2_p1, n7_segment_display_2_p1
  // BCD_to_7_Segment_decoder bcd_to_7_segment_decoder_2: pin names not known
  // _7_Segment_Display 7_segment_display_3: pin names not known; wires that end beside it: n7_segment_display_3_p1, n7_segment_display_3_p1
  // BCD_to_7_Segment_decoder bcd_to_7_segment_decoder_3: pin names not known

  // Notes on the sheet:
  //   Instructions Memory
  //   Register A
  //   Register B
endmodule
