// Logisim project class_exercises0.circ as structural Verilog: 1 circuit, main circuit main
module main (
  input  A_1,
  input  B_1,
  input  A_2,
  input  B_2,
  input  C_2,
  output out_6,
  output D
);

  wire and_1_out, and_2_out, and_3_out, and_4_out, and_5_out, and_6_out, and_7_out, and_8_out, and_9_out,
       and_10_out, not_1_out, not_2_out, not_3_out, or_2_out, or_3_out;

  not not_1 (not_1_out, A_1);
  not not_2 (not_2_out, A_2);
  not not_3 (not_3_out, C_2);
  and and_1 (and_1_out, not_1_out, B_1);
  and and_2 (and_2_out, A_1, B_1);
  and and_3 (and_3_out, not_2_out, B_2);
  and and_4 (and_4_out, not_2_out, B_2);
  and and_5 (and_5_out, A_2, B_2);
  and and_6 (and_6_out, A_2, B_2);
  or or_1 (out_6, and_1_out, and_2_out);
  and and_7 (and_7_out, and_3_out, not_3_out);
  and and_8 (and_8_out, and_4_out, C_2);
  and and_9 (and_9_out, and_5_out, not_3_out);
  and and_10 (and_10_out, and_6_out, C_2);
  or or_2 (or_2_out, and_7_out, and_8_out);
  or or_3 (or_3_out, or_2_out, and_9_out);
  or or_4 (D, or_3_out, and_10_out);

  // Notes on the sheet:
  //   D = F(A,B,C) = (`A * B * `C) + (`A * B * C) + (A * B * `C) + (A * B * C)
endmodule
