// Logisim project d_latch.circ as structural Verilog: 3 circuits, main circuit main
module main (
  input  [3:0] in_1,
  output [3:0] out_2
);

  wire clock_1_out;

  Clock clock_1 (.out(clock_1_out));
  DFLIPFLOP dflipflop_1 (.D(in_1[0]), .C(clock_1_out), .Q(out_2[0]));  // open: notQ
  DFLIPFLOP dflipflop_2 (.D(in_1[1]), .C(clock_1_out), .Q(out_2[1]));  // open: notQ
  DFLIPFLOP dflipflop_3 (.D(in_1[2]), .C(clock_1_out), .Q(out_2[2]));  // open: notQ
  DFLIPFLOP dflipflop_4 (.D(in_1[3]), .C(clock_1_out), .Q(out_2[3]));  // open: notQ
endmodule

module DLATCH (
  input  C,
  input  D,
  output Q,
  output notQ
);

  wire and_1_out, and_2_out, not_1_out;

  not not_1 (not_1_out, D);
  and and_1 (and_1_out, C, not_1_out);
  and and_2 (and_2_out, C, D);
  nor nor_1 (Q, and_1_out, notQ);
  nor nor_2 (notQ, Q, and_2_out);
endmodule

module DFLIPFLOP (
  input  D,
  input  C,
  output Q,
  output notQ
);

  wire dlatch_1_q, not_1_out;

  not not_1 (not_1_out, C);
  DLATCH dlatch_1 (.C(C), .D(D), .Q(dlatch_1_q));  // open: notQ
  DLATCH dlatch_2 (.C(not_1_out), .D(dlatch_1_q), .Q(Q), .notQ(notQ));
endmodule
