// Logisim project intro.circ as structural Verilog: 1 circuit, main circuit main
module main (
  input  in_1,
  input  in_2,
  input  in_3,
  input  in_4,
  input  in_5,
  input  in_6,
  input  in_7,
  input  in_8,
  input  in_9,
  input  in_10,
  input  in_11,
  input  in_12,
  input  in_13,
  input  in_14,
  input  NOR,
  input  A,
  input  B,
  output out_18,
  output out_19,
  output out_20,
  output out_21,
  output out_22,
  output out_23,
  output out_24,
  output out_25,
  output out_26,
  output out_27,
  output out_28
);

  wire and_2_out, and_4_out, and_5_out, not_1_out, not_2_out, not_3_out, not_4_out, or_2_out;

  and and_1 (out_20, in_5, in_8);
  nand nand_1 (out_23, in_12, in_14);
  not not_1 (not_1_out, A);
  not not_2 (not_2_out, B);
  not not_3 (not_3_out, A);
  not not_4 (not_4_out, B);
  and and_2 (and_2_out, A, B);
  or or_1 (out_26, not_1_out, not_2_out);
  or or_2 (or_2_out, A, B);
  and and_3 (out_28, not_3_out, not_4_out);
  and and_4 (and_4_out, in_2, in_3);
  not not_5 (out_25, and_2_out);
  not not_6 (out_27, or_2_out);
  and and_5 (and_5_out, and_4_out, in_4);
  or or_3 (out_21, in_6, in_9);
  nor nor_1 (out_24, in_13, NOR);
  xor xor_1 (out_18, in_1, and_5_out);
  not not_7 (out_19, in_7);
  xor xor_2 (out_22, in_10, in_11);

  // Notes on the sheet:
  //   AND
  //   NAND
  //   DeMorgan's Proof
  //   OR
  //   NOT
  //   XOR
endmodule
