// Logisim project sample_problem.circ as structural Verilog: 1 circuit, main circuit main
module main (
  input  A,
  input  B,
  input  C,
  output F,
  output E
);

  wire and_1_out, and_2_out, and_3_out, and_4_out, and_6_out, and_7_out, and_8_out, not_1_out, not_2_out,
       not_3_out, or_1_out;

  and and_1 (and_1_out, A, B);
  not not_1 (not_1_out, A);
  and and_2 (and_2_out, not_1_out, B);
  and and_3 (and_3_out, A, not_2_out);
  not not_2 (not_2_out, B);
  and and_4 (and_4_out, A, B);
  and and_5 (F, and_1_out, C);
  and and_6 (and_6_out, and_2_out, C);
  and and_7 (and_7_out, and_3_out, C);
  and and_8 (and_8_out, and_4_out, not_3_out);
  not not_3 (not_3_out, C);
  or or_1 (or_1_out, and_6_out, and_7_out);
  or or_2 (E, or_1_out, and_8_out);
endmodule
