// Logisim project var3_10.circ as structural Verilog: 1 circuit, main circuit main
module main (
  input  a,
  input  c,
  input  b,
  output out_4,
  output out_5
);

  wire and_1_out, and_2_out, not_1_out, not_2_out;

  not not_1 (not_1_out, c);
  not not_2 (not_2_out, a);
  and and_1 (and_1_out, a, not_1_out);
  and and_2 (and_2_out, not_2_out, c);
  or or_1 (out_4, and_1_out, and_2_out);

  assign out_5 = b;

  // Notes on the sheet:
  //   f(a,b,c) = a`c + `ac
endmodule
