// Logisim project var3_7.circ as structural Verilog: 1 circuit, main circuit main
module main (
  input  a,
  input  b,
  input  c,
  input  a_1,
  input  b_1,
  input  c_1,
  output out_7,
  output out_8
);

  wire and_1_out, and_2_out, and_3_out, and_4_out, and_5_out, and_6_out, and_7_out, and_8_out, and_9_out,
       and_10_out, not_1_out, not_2_out, not_3_out, not_4_out, not_5_out, or_2_out, or_3_out;

  not not_1 (not_1_out, a);
  not not_2 (not_2_out, b);
  not not_3 (not_3_out, c);
  not not_4 (not_4_out, c_1);
  not not_5 (not_5_out, b_1);
  and and_1 (and_1_out, not_1_out, not_2_out);
  and and_2 (and_2_out, not_1_out, b);
  and and_3 (and_3_out, a, not_2_out);
  and and_4 (and_4_out, a, b);
  and and_5 (and_5_out, b_1, not_4_out);
  and and_6 (and_6_out, not_5_out, c_1);
  and and_7 (and_7_out, and_1_out, c);
  and and_8 (and_8_out, and_2_out, not_3_out);
  and and_9 (and_9_out, and_3_out, c);
  and and_10 (and_10_out, and_4_out, not_3_out);
  or or_1 (out_8, and_5_out, and_6_out);
  or or_2 (or_2_out, and_7_out, and_8_out);
  or or_3 (or_3_out, or_2_out, and_9_out);
  or or_4 (out_7, or_3_out, and_10_out);
endmodule
