// Logisim project var3_9.circ as structural Verilog: 1 circuit, main circuit main
module main (
  input  a,
  input  b,
  input  c,
  output out_4
);

  wire and_1_out, not_1_out, not_2_out, not_3_out;

  not not_1 (not_1_out, a);
  not not_2 (not_2_out, b);
  not not_3 (not_3_out, c);
  and and_1 (and_1_out, not_1_out, not_2_out);
  or or_1 (out_4, and_1_out, not_3_out);

  // Notes on the sheet:
  //   f(a,b,c) = `c + `a`b
endmodule
